# Fritzing sketch Task1_ButtonToLed (saved by Fritzing 0.8.7b)
breadboards: 1

parts:
  S1 = Pushbutton [package="[THT]"]
  Arduino_1 = Arduino Uno (Rev3)
  LED1 = LED - 5mm [color="Red (660nm)" package="5 mm [THT]"]
  R1 = Resistor [tolerance=±5% resistance=220 package=THT]

nets:
  N1: S1.Pin_1, S1.Pin_2, Arduino_1.GND, LED1.cathode
  N2: S1.Pin_3, S1.Pin_4, Arduino_1.D2
  N3: Arduino_1.D3_PWM, R1.Pin_1
  N4: LED1.anode, R1.Pin_0
