# Fritzing sketch Task2_ConnectToTheCloud (saved by Fritzing 0.8.7b)
breadboards: 1

parts:
  Arduino_1 = Arduino Uno (Rev3)
  NRF24L1 = NRF24L01
  LED1 = LED - 5mm [color="Red (660nm)" package="5 mm [THT]"]
  R1 = Resistor [tolerance=±5% resistance=220 package=THT]
  S1 = Pushbutton [package="[THT]"]

nets:
  N1: Arduino_1.D9_PWM, NRF24L1.CE
  N2: Arduino_1.D10_PWM/SS, NRF24L1.CSN
  N3: Arduino_1.D11_PWM/MOSI, NRF24L1.MOSI
  N4: Arduino_1.D12/MISO, NRF24L1.MISO
  N5: Arduino_1.D13/SCK, NRF24L1.SCK
  GND: Arduino_1.GND, NRF24L1.GND, LED1.cathode, S1.Pin_1, S1.Pin_2
  N6: Arduino_1.D2, S1.Pin_3, S1.Pin_4
  N7: Arduino_1.D3_PWM, R1.Pin_1
  3V3: Arduino_1.3V3, NRF24L1.VCC
  N8: LED1.anode, R1.Pin_0

custom parts:
  NRF24L01: NRF24L01 module
